// Logisim project Pipelined_CPU.circ as structural Verilog: 6 circuits, main circuit main
module main (
);

  wire ALUSrc, Beqz, Bgez, Bgtz, Blez, Bltz, Bnez, clock, EX_MemRead, EX_RegWrite, ExtOp, j, jal, Jalr, jr,
       Kill1, Kill2, MEM_RegWrite, MemRead, MemtoReg, MemWrt, not_1_out, not_2_out, or_3_out, RegDest,
       register_4_q, register_5_q, register_6_q, RegWrite, SET, Sign, SSET, SSET_SET, SSET_SET_Jump, Stall,
       Zero;
  wire [1:0] f, ForwardA, ForwardB, PCSrcP;
  wire [2:0] multiplexer_1_out, multiplexer_2_out, multiplexer_4_out, Rb, RD2, RD3, RD4, RS, RT;
  wire [3:0] ALUCtrl, Branches;
  wire [4:0] OpCode;
  wire [4:2] Imm5;
  wire [7:0] Imm8R;
  wire [7:5] Imm8;
  wire [8:7] EX_q;
  wire [10:0] controunit_1_regwrite, Imm11R;
  wire [10:8] Imm11;
  wire [14:0] multiplexer_15_out;
  wire [15:0] multiplexer_5_out, rom_1_data;
  wire [19:0] adder_1_out, adder_2_out, bit_extender_2_out, bit_extender_3_out, branch, ExtImm8, ExtImm11,
       jump, jumpR, multiplexer_3_out, PC, PC_1R;
  wire [31:0] A, ALU__OUT, ALU_Result, AM, B, B_ALU, b_t, bit_extender_4_out, bit_extender_5_out,
       bit_extender_8_out, BusW, DR_q, ExtendedImm5, Imm5R_q, multiplexer_7_out, multiplexer_9_out,
       multiplexer_10_out, multiplexer_12_out, multiplexer_13_out, PC_1, ram_1_data, RbDR, Result;

  assign PC_1 = {{12{1'b0}}, adder_1_out};  // Bit_Extender bit_extender_1
  Adder #(.width(20)) adder_1 (.a(20'h1), .b(PC), .out(adder_1_out));  // open: cin, cout
  assign bit_extender_2_out = {{12{Imm8R[7]}}, Imm8R};  // Bit_Extender bit_extender_2
  Bit_Extender #(.in_width(32), .out_width(20)) bit_extender_3 (.in(A), .out(bit_extender_3_out));
  Multiplexer #(.width(3), .enable("false")) multiplexer_1 (
    .in0(Imm5), .in1(multiplexer_2_out), .out(multiplexer_1_out), .sel(SSET_SET_Jump));
  Multiplexer #(.width(3), .enable("false")) multiplexer_2 (
    .in0(3'b111), .in1(3'b000), .out(multiplexer_2_out), .sel(SSET_SET));
  ROM #(.addrWidth(20), .dataWidth(16)) rom_1 (.addr(PC), .data(rom_1_data));  // open: sel
  Clock clock_1 (.out(clock));
  Register #(.width(20)) NPCR (.D(adder_1_out), .en(1'b1), .Q(PC_1R), .clk(clock));  // open: clr
  Register #(.width(20)) register_1 (.D(multiplexer_3_out), .en(not_1_out), .Q(PC), .clk(clock));  // open: clr
  Multiplexer #(.select(2), .width(20), .enable("false")) multiplexer_3 (
    .in0(adder_1_out), .in1(jump), .in2(branch), .in3(jumpR), .out(multiplexer_3_out), .sel(PCSrcP));
  not not_1 (not_1_out, Stall);
  Adder #(.width(20)) adder_2 (.a(PC), .b(bit_extender_2_out), .out(adder_2_out));  // open: cin, cout
  Register #(.width(20), .trigger("low")) BTAR (.D(adder_2_out), .Q(branch), .clk(clock));  // open: en, clr
  Adder #(.width(20)) adder_3 (.a(PC), .b(ExtImm11), .out(jump));  // open: cin, cout
  Adder #(.width(20)) adder_4 (.a(bit_extender_2_out), .b(bit_extender_3_out), .out(jumpR));  // open: cin, cout
  Multiplexer #(.width(3), .enable("false")) multiplexer_4 (
    .in0(Rb), .in1(multiplexer_1_out), .out(multiplexer_4_out), .sel(RegDest));
  Multiplexer #(.width(16), .enable("false")) multiplexer_5 (
    .in0(rom_1_data), .in1({16{1'b0}}), .out(multiplexer_5_out), .sel(Kill1));
  Register #(.width(3)) Rd2R (.D(multiplexer_4_out), .en(1'b1), .Q(RD2), .clk(clock));  // open: clr
  Register #(.width(16)) InstR (
    .D(multiplexer_5_out), .en(not_2_out), .Q({OpCode, Imm11, Imm8, Imm5, f}), .clk(clock));  // open: clr
  not not_2 (not_2_out, Stall);
  Multiplexer #(.width(3), .enable("false")) multiplexer_6 (.in0(Imm8), .in1(3'b000), .out(Rb), .sel(SSET));
  or or_1 (SSET_SET, SET, SSET);
  Register #(.width(3)) Rd3R (.D(RD2), .en(1'b1), .Q(RD3), .clk(clock));  // open: clr
  Register #(.width(3)) register_2 (.D(Imm11), .en(1'b1), .Q(RS), .clk(clock));  // open: clr
  Register #(.width(3)) register_3 (.D(Rb), .en(1'b1), .Q(RT), .clk(clock));  // open: clr
  or or_2 (SSET_SET_Jump, SET, SSET, jal, Jalr);
  Register #(.width(3)) Rd4R (.D(RD3), .en(1'b1), .Q(RD4), .clk(clock));  // open: clr
  Register #(.width(1)) register_4 (.D(SSET_SET_Jump), .en(1'b1), .Q(register_4_q), .clk(clock));  // open: clr
  Register #(.width(1)) register_5 (.D(SSET_SET), .en(1'b1), .Q(register_5_q), .clk(clock));  // open: clr
  Register #(.width(1)) register_6 (.D(SSET), .en(1'b1), .Q(register_6_q), .clk(clock));  // open: clr
  assign bit_extender_4_out = {{27{1'b0}}, {Imm5, f}};  // Bit_Extender bit_extender_4
  assign bit_extender_5_out = {{27{Imm5[4]}}, {Imm5, f}};  // Bit_Extender bit_extender_5
  Register #(.width(11)) register_7 (.D({Imm11, Imm8, Imm5, f}), .Q(Imm11R), .clk(clock));  // open: en, clr
  assign ExtImm11 = {{9{Imm11R[10]}}, Imm11R};  // Bit_Extender bit_extender_6
  assign ExtImm8 = {{12{Imm8R[7]}}, Imm8R};  // Bit_Extender bit_extender_7
  Register register_8 (.D({Imm8, Imm5, f}), .Q(Imm8R), .clk(clock));  // open: en, clr
  Multiplexer #(.select(2), .width(32), .enable("false")) multiplexer_7 (
    .in0(B), .in1(ALU__OUT), .in2(RbDR), .in3(BusW), .out(multiplexer_7_out), .sel(ForwardB));
  Register #(.width(32)) Imm5R (.D(ExtendedImm5), .en(1'b1), .Q(Imm5R_q), .clk(clock));  // open: clr
  Multiplexer #(.width(32), .enable("false")) multiplexer_8 (
    .in0(ALU_Result), .in1(multiplexer_9_out), .out(ALU__OUT), .sel(register_4_q));
  Multiplexer #(.width(32), .enable("false")) multiplexer_9 (
    .in0(PC_1), .in1(multiplexer_10_out), .out(multiplexer_9_out), .sel(register_5_q));
  Multiplexer #(.width(32), .enable("false")) multiplexer_10 (
    .in0(bit_extender_8_out), .in1({ALU_Result[31:11], Imm11R}), .out(multiplexer_10_out), .sel(register_6_q));
  assign bit_extender_8_out = {{12{ExtImm11[19]}}, ExtImm11};  // Bit_Extender bit_extender_8
  Multiplexer #(.width(32), .enable("false")) multiplexer_11 (
    .in0(bit_extender_4_out), .in1(bit_extender_5_out), .out(ExtendedImm5), .sel(ExtOp));
  Multiplexer #(.select(2), .width(32), .enable("false")) multiplexer_12 (
    .in0(A), .in1(ALU__OUT), .in2(RbDR), .in3(BusW), .out(multiplexer_12_out), .sel(ForwardA));
  Multiplexer #(.width(32), .enable("false")) multiplexer_13 (
    .in0(b_t), .in1(Imm5R_q), .out(multiplexer_13_out), .sel(ALUSrc));
  RegisterFile registerfile_1 (
    .RA(Imm11), .RB(Rb), .RegWrite(RegWrite), .RW(RD4), .BusA(A), .BusB(B), .BusW(BusW), .CLK(clock));
  Register #(.width(32)) AR (.D(multiplexer_12_out), .en(1'b1), .Q(AM), .clk(clock));  // open: clr
  Register #(.width(32)) BR (.D(multiplexer_7_out), .en(1'b1), .Q(b_t), .clk(clock));  // open: clr
  Multiplexer #(.width(32), .enable("false")) multiplexer_14 (
    .in0(multiplexer_13_out), .in1(32'hb), .out(B_ALU), .sel(SSET));
  PCNext pcnext_1 (
    .Bgtz(Bgtz), .Zero(Zero), .Bnez(Bnez), .Beqz(Beqz), .Bgez(Bgez), .Bltz(Bltz), .Blez(Blez), .Sign(Sign),
    .PCSrc(PCSrcP), .Kill1(Kill1), .Kill2(Kill2), .jal(jal), .JALR(Jalr), .jump(j), .Jr(jr));
  ALU alu_1 (.A(AM), .B(B_ALU), .ALU_out(ALU_Result), .ALUCntl(ALUCtrl), .Sign(Sign), .Zero(Zero));
  HazardControl hazardcontrol_1 (
    .EX_MemRead(EX_MemRead), .ForwardA(ForwardA), .EX_RegWrite(EX_RegWrite), .ForwardB(ForwardB),
    .MEM_RegWrite(MEM_RegWrite), .Stall(Stall), .WB_RegWrite(RegWrite), .RS0(Imm11), .RT0(Imm8), .RD2(RD2),
    .RD3(RD3), .RD4(RD4));
  Register #(.width(32)) RR (.D(ALU__OUT), .en(1'b1), .Q(Result), .clk(clock));  // open: clr
  Multiplexer #(.width(15), .disabled(0), .enable("false")) multiplexer_15 (
    .in0({Branches, controunit_1_regwrite}), .in1({15{1'b0}}), .out(multiplexer_15_out), .sel(or_3_out));
  or or_3 (or_3_out, Stall, Kill2);
  Register #(.width(32)) DR (.D(B), .en(1'b1), .Q(DR_q), .clk(clock));  // open: clr
  Register #(.width(15)) EX (
    .D(multiplexer_15_out), .en(1'b1),
    .Q({Blez, Bgtz, Bgez, Bltz, Beqz, Bnez, EX_q, EX_MemRead, ALUCtrl, ALUSrc, EX_RegWrite}), .clk(clock));  // open: clr
  ControUnit controunit_1 (
    .RegDst(RegDest), .RegWrite(controunit_1_regwrite[0]), .ExtOp(ExtOp), .ALUSrc(controunit_1_regwrite[1]),
    .Beqz(controunit_1_regwrite[10]), .Bnez(controunit_1_regwrite[9]), .MemRead(controunit_1_regwrite[6]),
    .ALUCtrl(controunit_1_regwrite[5:2]), .MemWrite(controunit_1_regwrite[7]),
    .MemtoReg(controunit_1_regwrite[8]), .J(j), .Jal(jal), .Jr(jr), .Bltz(Branches[0]), .Bgez(Branches[1]),
    .Bgtz(Branches[2]), .Blez(Branches[3]), .Jalr(Jalr), .SET(SET), .SSET(SSET), .Function(f), .OpCode(OpCode));
  RAM #(.addrWidth(20), .dataWidth(32), .bus("separate")) ram_1 (
    .addr(Result[19:0]), .din(DR_q), .data(ram_1_data), .str(MemWrt), .clk(clock), .ld(MemRead));  // open: sel, clr
  Multiplexer #(.width(32), .enable("false")) multiplexer_16 (
    .in0(Result), .in1(ram_1_data), .out(RbDR), .sel(MemtoReg));
  Register #(.width(4)) MEM (
    .D({EX_q, EX_MemRead, EX_RegWrite}), .en(1'b1), .Q({MemtoReg, MemWrt, MemRead, MEM_RegWrite}), .clk(clock));  // open: clr
  Register #(.width(32)) DataR (.D(RbDR), .en(1'b1), .Q(BusW), .clk(clock));  // open: clr
  Register #(.width(1)) WB (.D(MEM_RegWrite), .en(1'b1), .Q(RegWrite), .clk(clock));  // open: clr

  // Other names for the same wires on the sheet: Imm5[1:0] = f; Imm8[4:0] = {Imm5, f}; Imm11[7:0] = {Imm8, Imm5, f};
  //   Rd[2:0] = Imm5; Rt_t[2:0] = Imm8; Rs_t[2:0] = Imm11; EX_Branches[5:0] = {Blez, Bgtz, Bgez, Bltz, Beqz, Bnez};
  //   BusWM[31:0] = BusW; RaDR[31:0] = BusW; Rw[2:0] = RD4; WB_RegWrite = RegWrite

  // Notes on the sheet:
  //   Instruction_Memorey
  //   contents of rom_1 (hex, n*v repeats v):
  //   24b 8020 2161 a68 6921 a9fb
  //   Main
  //   HazardControl
  //   PCNext
  //   PCNext
  //   PCNext
  //   ControlUnit
  //   ControlUnit
  //   Data_Memory
endmodule

module RegisterFile (
  input  [2:0] RA,
  input  [2:0] RB,
  input  [31:0] BusW,
  input  [2:0] RW,
  input  RegWrite,
  input  CLK,
  output [31:0] BusA,
  output [31:0] BusB
);

  wire and_1_out, and_2_out, and_3_out, and_4_out, and_5_out, and_6_out, and_7_out, and_8_out,
       decoder_1_out0, decoder_1_out1, decoder_1_out2, decoder_1_out3, decoder_1_out4, decoder_1_out5,
       decoder_1_out6, decoder_1_out7, decoder_2_out0, decoder_2_out1, decoder_2_out2, decoder_2_out3,
       decoder_2_out4, decoder_2_out5, decoder_2_out6, decoder_2_out7, decoder_3_out0, decoder_3_out1,
       decoder_3_out2, decoder_3_out3, decoder_3_out4, decoder_3_out5, decoder_3_out6, decoder_3_out7;
  wire [31:0] R0_q, R1_q, R2_q, R3_q, R4_q, R5_q, R6_q, R7_q;

  Decoder #(.select(3), .enable("false")) decoder_1 (
    .out0(decoder_1_out0), .out1(decoder_1_out1), .out2(decoder_1_out2), .out3(decoder_1_out3),
    .out4(decoder_1_out4), .out5(decoder_1_out5), .out6(decoder_1_out6), .out7(decoder_1_out7), .sel(RW));
  and and_1 (and_1_out, decoder_1_out0, RegWrite);
  and and_2 (and_2_out, decoder_1_out1, RegWrite);
  and and_3 (and_3_out, decoder_1_out2, RegWrite);
  and and_4 (and_4_out, decoder_1_out3, RegWrite);
  and and_5 (and_5_out, decoder_1_out4, RegWrite);
  and and_6 (and_6_out, decoder_1_out5, RegWrite);
  and and_7 (and_7_out, decoder_1_out6, RegWrite);
  and and_8 (and_8_out, decoder_1_out7, RegWrite);
  Register #(.width(32)) R0 (.D(BusW), .en(and_1_out), .Q(R0_q), .clk(CLK));  // open: clr
  Register #(.width(32)) R1 (.D(BusW), .en(and_2_out), .Q(R1_q), .clk(CLK));  // open: clr
  Register #(.width(32)) R2 (.D(BusW), .en(and_3_out), .Q(R2_q), .clk(CLK));  // open: clr
  Register #(.width(32)) R3 (.D(BusW), .en(and_4_out), .Q(R3_q), .clk(CLK));  // open: clr
  Register #(.width(32)) R4 (.D(BusW), .en(and_5_out), .Q(R4_q), .clk(CLK));  // open: clr
  Register #(.width(32)) R5 (.D(BusW), .en(and_6_out), .Q(R5_q), .clk(CLK));  // open: clr
  Register #(.width(32)) R6 (.D(BusW), .en(and_7_out), .Q(R6_q), .clk(CLK));  // open: clr
  Register #(.width(32)) R7 (.D(BusW), .en(and_8_out), .Q(R7_q), .clk(CLK));  // open: clr
  // Probe on BusA
  Decoder #(.select(3), .enable("false")) decoder_2 (
    .out0(decoder_2_out0), .out1(decoder_2_out1), .out2(decoder_2_out2), .out3(decoder_2_out3),
    .out4(decoder_2_out4), .out5(decoder_2_out5), .out6(decoder_2_out6), .out7(decoder_2_out7), .sel(RA));
  assign BusA = decoder_2_out0 ? R0_q : 32'bz;  // Controlled_Buffer controlled_buffer_1
  assign BusA = decoder_2_out1 ? R1_q : 32'bz;  // Controlled_Buffer controlled_buffer_2
  assign BusA = decoder_2_out2 ? R2_q : 32'bz;  // Controlled_Buffer controlled_buffer_3
  assign BusA = decoder_2_out3 ? R3_q : 32'bz;  // Controlled_Buffer controlled_buffer_4
  assign BusA = decoder_2_out4 ? R4_q : 32'bz;  // Controlled_Buffer controlled_buffer_5
  assign BusA = decoder_2_out5 ? R5_q : 32'bz;  // Controlled_Buffer controlled_buffer_6
  assign BusA = decoder_2_out6 ? R6_q : 32'bz;  // Controlled_Buffer controlled_buffer_7
  assign BusA = decoder_2_out7 ? R7_q : 32'bz;  // Controlled_Buffer controlled_buffer_8
  Decoder #(.select(3), .enable("false")) decoder_3 (
    .out0(decoder_3_out0), .out1(decoder_3_out1), .out2(decoder_3_out2), .out3(decoder_3_out3),
    .out4(decoder_3_out4), .out5(decoder_3_out5), .out6(decoder_3_out6), .out7(decoder_3_out7), .sel(RB));
  assign BusB = decoder_3_out0 ? R0_q : 32'bz;  // Controlled_Buffer controlled_buffer_9
  assign BusB = decoder_3_out1 ? R1_q : 32'bz;  // Controlled_Buffer controlled_buffer_10
  assign BusB = decoder_3_out2 ? R2_q : 32'bz;  // Controlled_Buffer controlled_buffer_11
  assign BusB = decoder_3_out3 ? R3_q : 32'bz;  // Controlled_Buffer controlled_buffer_12
  assign BusB = decoder_3_out4 ? R4_q : 32'bz;  // Controlled_Buffer controlled_buffer_13
  assign BusB = decoder_3_out5 ? R5_q : 32'bz;  // Controlled_Buffer controlled_buffer_14
  assign BusB = decoder_3_out6 ? R6_q : 32'bz;  // Controlled_Buffer controlled_buffer_15
  assign BusB = decoder_3_out7 ? R7_q : 32'bz;  // Controlled_Buffer controlled_buffer_16
  // Probe on BusB
endmodule

module ALU (
  input  [31:0] A,
  input  [31:0] B,
  input  [3:0] ALUCntl,
  output [31:0] ALU_out,
  output Sign,
  output Zero
);

  wire comparator_2_lt, comparator_3_lt, multiplexer_2_out;
  wire [31:0] adder_1_out, AND_out, bit_extender_1_out, bit_extender_2_out, CAND_out, multiplexer_1_out,
       multiplexer_3_out, not_1_out, OR_out, shifter_1_out, shifter_2_out, shifter_3_out, shifter_4_out,
       xor_1_out, XOR_2_out;

  // Probe on B
  assign bit_extender_1_out = {{31{ALUCntl[2]}}, ALUCntl[2]};  // Bit_Extender bit_extender_1
  // Probe on A
  assign xor_1_out = A ^ bit_extender_1_out;  // XOR_Gate xor_1, 32 bits wide
  assign not_1_out = ~A;  // NOT_Gate not_1, 32 bits wide
  Comparator #(.width(32)) comparator_1 (.a(A), .b({32{1'b0}}), .eq(Zero));  // open: gt, lt
  Adder #(.width(32)) adder_1 (.a(B), .b(xor_1_out), .out(adder_1_out), .cin(ALUCntl[2]));  // open: cout
  // Probe on adder_1_out
  assign CAND_out = not_1_out & B;  // AND_Gate CAND, 32 bits wide
  assign AND_out = A & B;  // AND_Gate AND, 32 bits wide
  assign OR_out = A | B;  // OR_Gate OR, 32 bits wide
  assign XOR_2_out = A ^ B;  // XOR_Gate XOR_2, 32 bits wide
  Multiplexer #(.select(2), .width(32), .enable("false")) multiplexer_1 (
    .in0(AND_out), .in1(CAND_out), .in2(OR_out), .in3(XOR_2_out), .out(multiplexer_1_out), .sel(ALUCntl[3:2]));
  Comparator #(.width(32)) comparator_2 (.a(A), .b(B), .lt(comparator_2_lt));  // open: gt, eq
  Comparator #(.width(32), .mode("unsigned")) comparator_3 (.a(A), .b(B), .lt(comparator_3_lt));  // open: gt, eq
  Shifter #(.width(32), .shift("rr")) shifter_1 (.in(A), .\dist (B[4:0]), .out(shifter_1_out));
  Shifter #(.width(32)) shifter_2 (.in(A), .\dist (B[4:0]), .out(shifter_2_out));
  Shifter #(.width(32), .shift("lr")) shifter_3 (.in(A), .\dist (B[4:0]), .out(shifter_3_out));
  Shifter #(.width(32), .shift("ar")) shifter_4 (.in(A), .\dist (B[4:0]), .out(shifter_4_out));
  Multiplexer #(.enable("false")) multiplexer_2 (
    .in0(comparator_2_lt), .in1(comparator_3_lt), .out(multiplexer_2_out), .sel(ALUCntl[2]));
  assign bit_extender_2_out = {{31{1'b0}}, multiplexer_2_out};  // Bit_Extender bit_extender_2
  Multiplexer #(.select(2), .width(32), .enable("false")) multiplexer_3 (
    .in0(shifter_1_out), .in1(shifter_2_out), .in2(shifter_3_out), .in3(shifter_4_out),
    .out(multiplexer_3_out), .sel(ALUCntl[3:2]));
  // Probe on multiplexer_3_out
  Multiplexer #(.select(2), .width(32), .enable("false")) multiplexer_4 (
    .in0(multiplexer_3_out), .in1(bit_extender_2_out), .in2(adder_1_out), .in3(multiplexer_1_out),
    .out(ALU_out), .sel(ALUCntl[1:0]));

  assign Sign = ALU_out[31];

  // Other names for the same wires on the sheet: OP_1[1:0] = ALUCntl[3:2]; OP_3 = ALUCntl[2];
  //   OP_2[1:0] = ALUCntl[1:0]; ResultR[31:0] = ALU_out

  // Notes on the sheet:
  //   ADD = 0
  //   SUB = 1
  //   CAND = 00
  //   AND = 01
  //   OR = 10
  //   XOR = 11
  //   UnsignedOp
  //   SLT = 0
  //   SLTU = 1
  //   ROR = 00
  //   SLL = 01
  //   SRL = 10
  //   SRA = 11
  //   Shift = 00
  //   Slt = 01
  //   Add/ Sub = 10
  //   Logic = 11
endmodule

module PCNext (
  input  jal,
  input  JALR,
  input  jump,
  input  Jr,
  input  Bgtz,
  input  Zero,
  input  Bnez,
  input  Beqz,
  input  Bgez,
  input  Bltz,
  input  Blez,
  input  Sign,
  output [1:0] PCSrc,
  output Kill1,
  output Kill2
);

  wire and_1_out, and_2_out, and_3_out, and_4_out, and_5_out, and_6_out, and_7_out, and_8_out, and_9_out,
       nor_1_out, not_1_out, not_2_out, not_3_out, not_4_out, or_1_out, or_3_out, or_4_out;

  and and_1 (and_1_out, Bgtz, and_2_out);
  and and_2 (and_2_out, not_2_out, not_1_out);
  not not_1 (not_1_out, Zero);
  not not_2 (not_2_out, Sign);
  nor nor_1 (nor_1_out, and_9_out, Kill2, and_8_out);
  and and_3 (and_3_out, or_1_out, Blez);
  or or_1 (or_1_out, Zero, Sign);
  Priority_Encoder #(.select(2)) priority_encoder_1 (
    .in0(nor_1_out), .in1(and_8_out), .in2(Kill2), .in3(and_9_out), .out(PCSrc));
  or or_2 (Kill2, and_1_out, and_3_out, and_4_out, and_5_out, and_6_out, and_7_out);
  and and_4 (and_4_out, not_3_out, Bnez);
  not not_3 (not_3_out, Zero);
  and and_5 (and_5_out, Zero, Beqz);
  and and_6 (and_6_out, Bgez, not_4_out);
  and and_7 (and_7_out, Sign, Bltz);
  not not_4 (not_4_out, Sign);
  and and_8 (and_8_out, ~Kill2, or_3_out);  // AND_Gate
  or or_3 (or_3_out, jump, jal);
  and and_9 (and_9_out, ~Kill2, or_4_out);  // AND_Gate
  or or_4 (or_4_out, JALR, Jr);
  or or_5 (Kill1, and_8_out, and_9_out, Kill2);
endmodule

module ControUnit (
  input  [1:0] Function,
  input  [4:0] OpCode,
  output RegDst,
  output RegWrite,
  output ExtOp,
  output ALUSrc,
  output Beqz,
  output Bnez,
  output MemRead,
  output [3:0] ALUCtrl,
  output MemWrite,
  output MemtoReg,
  output J,
  output Jal,
  output Jr,
  output Bltz,
  output Bgez,
  output Bgtz,
  output Blez,
  output Jalr,
  output SET,
  output SSET
);

  wire nor_1_out, nor_2_out, not_1_out;
  wire [5:0] adder_1_out, bit_extender_1_out, multiplexer_1_out, multiplexer_2_out;

  assign bit_extender_1_out = {{1{1'b0}}, OpCode};  // Bit_Extender bit_extender_1
  Adder #(.width(6)) adder_1 (.a(bit_extender_1_out), .b(6'b000110), .out(adder_1_out));  // open: cin, cout
  Multiplexer #(.width(6), .enable("false")) multiplexer_1 (
    .in0(adder_1_out), .in1({4'b0001, Function}), .out(multiplexer_1_out), .sel(nor_1_out));
  nor nor_1 (nor_1_out, OpCode[4], OpCode[3], OpCode[2], OpCode[1], not_1_out);
  not not_1 (not_1_out, OpCode[0]);
  Multiplexer #(.width(6), .enable("false")) multiplexer_2 (
    .in0(multiplexer_1_out), .in1({4'b0000, Function}), .out(multiplexer_2_out), .sel(nor_2_out));
  nor nor_2 (nor_2_out, OpCode[4], OpCode[3], OpCode[2], OpCode[1], OpCode[0]);
  ROM #(.addrWidth(6), .dataWidth(23)) rom_1 (
    .addr(multiplexer_2_out),
    .data({SSET, SET, Jalr, Blez, Bgtz, Bgez, Bltz, Jr, Jal, J, MemtoReg, MemWrite, MemRead, Bnez, Beqz, ALUCtrl, ALUSrc, ExtOp, RegWrite, RegDst}));  // open: sel

  // Notes on the sheet:
  //   contents of rom_1 (hex, n*v repeats v):
  //   33 73 b3 f3 23 63 13 53 0 0 3e 7e be fe 2e 6e 1e 5e 4e 8e ce e 142e 82c 0 0 104 204 10004 20004
  //   40004 80004 8004 100007 20000f 40004b 2004 4007
endmodule

module HazardControl (
  input  EX_MemRead,
  input  EX_RegWrite,
  input  MEM_RegWrite,
  input  WB_RegWrite,
  input  [2:0] RS0,
  input  [2:0] RT0,
  input  [2:0] RD2,
  input  [2:0] RD3,
  input  [2:0] RD4,
  output [1:0] ForwardA,
  output [1:0] ForwardB,
  output Stall
);

  wire and_1_out, and_2_out, and_3_out, and_4_out, and_5_out, and_6_out, comparator_1_eq, comparator_2_eq,
       comparator_3_eq, comparator_4_eq, comparator_5_eq, comparator_6_eq, comparator_7_eq, comparator_8_eq,
       comparator_9_eq, comparator_10_eq, comparator_11_eq, comparator_12_eq, comparator_13_eq,
       comparator_14_eq, comparator_15_eq, comparator_16_eq, comparator_17_eq, comparator_18_eq,
       comparator_19_eq, comparator_20_eq, FalseCondA, FalseCondB, not_1_out, not_2_out, not_3_out,
       not_4_out, not_5_out, not_6_out, or_1_out;
  wire [1:0] multiplexer_1_out, multiplexer_2_out, multiplexer_3_out, multiplexer_4_out;

  Multiplexer #(.width(2), .enable("false")) multiplexer_1 (
    .in0(2'b00), .in1(2'b11), .out(multiplexer_1_out), .sel(and_6_out));
  Multiplexer #(.width(2), .enable("false")) multiplexer_2 (
    .in0(2'b00), .in1(2'b11), .out(multiplexer_2_out), .sel(and_3_out));
  Multiplexer #(.width(2), .enable("false")) multiplexer_3 (
    .in0(multiplexer_2_out), .in1(2'b10), .out(multiplexer_3_out), .sel(and_2_out));
  Comparator #(.width(3)) comparator_1 (.a(RS0), .b(RD2), .eq(comparator_1_eq));  // open: gt, lt
  Comparator #(.width(3)) comparator_2 (.a(RS0), .b(RD3), .eq(comparator_2_eq));  // open: gt, lt
  Comparator #(.width(3)) comparator_3 (.a(RS0), .b(RD4), .eq(comparator_3_eq));  // open: gt, lt
  Multiplexer #(.width(2), .enable("false")) multiplexer_4 (
    .in0(multiplexer_1_out), .in1(2'b10), .out(multiplexer_4_out), .sel(and_5_out));
  Comparator #(.width(3)) comparator_4 (.a(RT0), .b(RD2), .eq(comparator_4_eq));  // open: gt, lt
  Comparator #(.width(3)) comparator_5 (.a(RT0), .b(RD3), .eq(comparator_5_eq));  // open: gt, lt
  Comparator #(.width(3)) comparator_6 (.a(RT0), .b(RD4), .eq(comparator_6_eq));  // open: gt, lt
  Multiplexer #(.width(2), .enable("false")) multiplexer_5 (
    .in0(multiplexer_3_out), .in1(2'b01), .out(ForwardA), .sel(and_1_out));
  and and_1 (and_1_out, comparator_1_eq, EX_RegWrite);
  and and_2 (and_2_out, comparator_2_eq, MEM_RegWrite);
  and and_3 (and_3_out, comparator_3_eq, WB_RegWrite);
  Multiplexer #(.width(2), .enable("false")) multiplexer_6 (
    .in0(multiplexer_4_out), .in1(2'b01), .out(ForwardB), .sel(and_4_out));
  and and_4 (and_4_out, comparator_4_eq, EX_RegWrite);
  and and_5 (and_5_out, comparator_5_eq, MEM_RegWrite);
  and and_6 (and_6_out, comparator_6_eq, WB_RegWrite);
  Comparator #(.width(2)) comparator_7 (.a(ForwardA), .b(2'b01), .eq(comparator_7_eq));  // open: gt, lt
  Comparator #(.width(2)) comparator_8 (.a(2'b01), .b(ForwardB), .eq(comparator_8_eq));  // open: gt, lt
  or or_1 (or_1_out, comparator_7_eq, comparator_8_eq);
  not not_1 (not_1_out, comparator_9_eq);
  Comparator #(.width(3)) comparator_9 (.a(RS0), .b(RD2), .eq(comparator_9_eq));  // open: gt, lt
  not not_2 (not_2_out, comparator_10_eq);
  Comparator #(.width(3)) comparator_10 (.a(RS0), .b(RD3), .eq(comparator_10_eq));  // open: gt, lt
  not not_3 (not_3_out, comparator_11_eq);
  Comparator #(.width(3)) comparator_11 (.a(RS0), .b(RD4), .eq(comparator_11_eq));  // open: gt, lt
  Comparator #(.width(1)) comparator_12 (.a(EX_RegWrite), .b(1'b0), .eq(comparator_12_eq));  // open: gt, lt
  Comparator #(.width(1)) comparator_13 (.a(MEM_RegWrite), .b(1'b0), .eq(comparator_13_eq));  // open: gt, lt
  Comparator #(.width(1)) comparator_14 (.a(WB_RegWrite), .b(1'b0), .eq(comparator_14_eq));  // open: gt, lt
  and and_7 (Stall, EX_MemRead, or_1_out);
  or or_2 (FalseCondA, not_1_out, not_2_out, not_3_out, comparator_12_eq, comparator_13_eq, comparator_14_eq);
  Comparator #(.width(3)) comparator_15 (.a(RT0), .b(RD2), .eq(comparator_15_eq));  // open: gt, lt
  Comparator #(.width(3)) comparator_16 (.a(RT0), .b(RD3), .eq(comparator_16_eq));  // open: gt, lt
  Comparator #(.width(3)) comparator_17 (.a(RT0), .b(RD4), .eq(comparator_17_eq));  // open: gt, lt
  Comparator #(.width(1)) comparator_18 (.a(EX_RegWrite), .b(1'b0), .eq(comparator_18_eq));  // open: gt, lt
  Comparator #(.width(1)) comparator_19 (.a(MEM_RegWrite), .b(1'b0), .eq(comparator_19_eq));  // open: gt, lt
  Comparator #(.width(1)) comparator_20 (.a(WB_RegWrite), .b(1'b0), .eq(comparator_20_eq));  // open: gt, lt
  not not_4 (not_4_out, comparator_15_eq);
  not not_5 (not_5_out, comparator_16_eq);
  not not_6 (not_6_out, comparator_17_eq);
  or or_3 (FalseCondB, not_4_out, not_5_out, not_6_out, comparator_18_eq, comparator_19_eq, comparator_20_eq);

  // Notes on the sheet:
  //   In
  //   Out
  //   FalseCondition
  //   FalseCondition
endmodule
