// Logisim project Single_Cycle_CPU.circ as structural Verilog: 5 circuits, main circuit main
module main (
);

  wire ALUSrc, Beqz, Bgez, Bgtz, Blez, Bltz, Bnez, clock, ExtOp, j, jal, Jalr, jr, MemRead, MemtoReg, MemWrt,
       RegDest, RegWrite, SET, Sign, SSET, SSET_SET, SSET_SET_Jump, Zero;
  wire [1:0] f, PCSrcP;
  wire [2:0] multiplexer_2_out, multiplexer_4_out, Rb, Rw;
  wire [3:0] ALUCtrl;
  wire [4:0] OpCode;
  wire [4:2] Imm5;
  wire [7:5] Imm8;
  wire [10:8] Imm11;
  wire [19:0] adder_1_out, bit_extender_2_out, branch, ExtImm8, ExtImm11, jump, jumpR, multiplexer_1_out, PC;
  wire [31:0] A, B, B_ALU, bit_extender_3_out, bit_extender_4_out, bit_extender_5_out, BusW, BusWM,
       ExtendedImm5, multiplexer_7_out, multiplexer_8_out, multiplexer_9_out, PC_1, ram_1_data, Result;

  assign PC_1 = {{12{1'b0}}, adder_1_out};  // Bit_Extender bit_extender_1
  Bit_Extender #(.in_width(32), .out_width(20)) bit_extender_2 (.in(A), .out(bit_extender_2_out));
  ROM #(.addrWidth(20), .dataWidth(16)) rom_1 (.addr(PC), .data({OpCode, Imm11, Imm8, Imm5, f}));  // open: sel
  Clock clock_1 (.out(clock));
  Adder #(.width(20)) adder_1 (.a(20'h1), .b(PC), .out(adder_1_out));  // open: cin, cout
  Multiplexer #(.select(2), .width(20), .enable("false")) multiplexer_1 (
    .in0(adder_1_out), .in1(jump), .in2(branch), .in3(jumpR), .out(multiplexer_1_out), .sel(PCSrcP));
  Register #(.width(20)) register_1 (.D(multiplexer_1_out), .en(1'b1), .Q(PC), .clk(clock));  // open: clr
  Adder #(.width(20)) adder_2 (.a(PC), .b(ExtImm8), .out(branch));  // open: cin, cout
  Adder #(.width(20)) adder_3 (.a(PC), .b(ExtImm11), .out(jump));  // open: cin, cout
  Adder #(.width(20)) adder_4 (.a(ExtImm8), .b(bit_extender_2_out), .out(jumpR));  // open: cin, cout
  Multiplexer #(.width(3), .enable("false")) multiplexer_2 (
    .in0(3'b111), .in1(3'b000), .out(multiplexer_2_out), .sel(SSET_SET));
  or or_1 (SSET_SET, SET, SSET);
  Multiplexer #(.width(3), .enable("false")) multiplexer_3 (.in0(Imm8), .in1(3'b000), .out(Rb), .sel(SSET));
  Multiplexer #(.width(3), .enable("false")) multiplexer_4 (
    .in0(Imm5), .in1(multiplexer_2_out), .out(multiplexer_4_out), .sel(SSET_SET_Jump));
  or or_2 (SSET_SET_Jump, SET, SSET, jal, Jalr);
  RegisterFile registerfile_1 (
    .RA(Imm11), .RB(Rb), .RegWrite(RegWrite), .RW(Rw), .BusA(A), .BusB(B), .BusW(BusW), .CLK(clock));
  Multiplexer #(.width(3), .enable("false")) multiplexer_5 (.in0(Rb), .in1(multiplexer_4_out), .out(Rw), .sel(RegDest));
  Multiplexer #(.width(32), .enable("false")) multiplexer_6 (
    .in0(BusWM), .in1(multiplexer_8_out), .out(BusW), .sel(SSET_SET_Jump));
  assign bit_extender_3_out = {{12{ExtImm11[19]}}, ExtImm11};  // Bit_Extender bit_extender_3
  Multiplexer #(.width(32), .enable("false")) multiplexer_7 (
    .in0(B), .in1(ExtendedImm5), .out(multiplexer_7_out), .sel(ALUSrc));
  assign bit_extender_4_out = {{27{1'b0}}, {Imm5, f}};  // Bit_Extender bit_extender_4
  assign bit_extender_5_out = {{27{Imm5[4]}}, {Imm5, f}};  // Bit_Extender bit_extender_5
  assign ExtImm11 = {{9{Imm11[10]}}, {Imm11, Imm8, Imm5, f}};  // Bit_Extender bit_extender_6
  assign ExtImm8 = {{12{Imm8[7]}}, {Imm8, Imm5, f}};  // Bit_Extender bit_extender_7
  ALU alu_1 (.A(A), .B(B_ALU), .ALU_out(Result), .ALUCntl(ALUCtrl), .Sign(Sign), .Zero(Zero));
  Multiplexer #(.width(32), .enable("false")) multiplexer_8 (
    .in0(PC_1), .in1(multiplexer_9_out), .out(multiplexer_8_out), .sel(SSET_SET));
  Multiplexer #(.width(32), .enable("false")) multiplexer_9 (
    .in0(bit_extender_3_out), .in1({Result[31:11], Imm11, Imm8, Imm5, f}), .out(multiplexer_9_out), .sel(SSET));
  Multiplexer #(.width(32), .enable("false")) multiplexer_10 (
    .in0(bit_extender_4_out), .in1(bit_extender_5_out), .out(ExtendedImm5), .sel(ExtOp));
  Multiplexer #(.width(32), .enable("false")) multiplexer_11 (
    .in0(multiplexer_7_out), .in1(32'hb), .out(B_ALU), .sel(SSET));
  ControUnit controunit_1 (
    .RegDst(RegDest), .RegWrite(RegWrite), .ExtOp(ExtOp), .ALUSrc(ALUSrc), .Beqz(Beqz), .Bnez(Bnez),
    .MemRead(MemRead), .ALUCtrl(ALUCtrl), .MemWrite(MemWrt), .MemtoReg(MemtoReg), .J(j), .Jal(jal), .Jr(jr),
    .Bltz(Bltz), .Bgez(Bgez), .Bgtz(Bgtz), .Blez(Blez), .Jalr(Jalr), .SET(SET), .SSET(SSET), .Function(f),
    .OpCode(OpCode));
  PCNext pcnext_1 (
    .PCSrc(PCSrcP), .Bgtz(Bgtz), .Sign(Sign), .Zero(Zero), .Blez(Blez), .Bnez(Bnez), .Beqz(Beqz),
    .Bgez(Bgez), .JALR(Jalr), .Bltz(Bltz), .jump(j), .Jr(jr), .jal(jal));
  RAM #(.addrWidth(20), .dataWidth(32), .bus("separate")) ram_1 (
    .addr(Result[19:0]), .din(B), .data(ram_1_data), .str(MemWrt), .clk(clock), .ld(MemRead));  // open: sel, clr
  Multiplexer #(.width(32), .enable("false")) multiplexer_12 (
    .in0(Result), .in1(ram_1_data), .out(BusWM), .sel(MemtoReg));

  // Other names for the same wires on the sheet: Imm5[1:0] = f; Imm8[4:0] = {Imm5, f}; Imm11[7:0] = {Imm8, Imm5, f};
  //   Rd[2:0] = Imm5; Rt[2:0] = Imm8; Rs[2:0] = Imm11

  // Notes on the sheet:
  //   Instruction_Memorey
  //   contents of rom_1 (hex, n*v repeats v):
  //   e007 a00f 127 835 a50a 4140 8260 8281 c7a a603 8a80 8a61 4121 f7f6 401f f7f2 47e1
  //   Main
  //   ControlUnit
  //   PCNext
  //   Data_Memory
  //   ControlUnit
  //   PCNext
endmodule

module RegisterFile (
  input  [2:0] RA,
  input  [2:0] RB,
  input  [31:0] BusW,
  input  [2:0] RW,
  input  RegWrite,
  input  CLK,
  output [31:0] BusA,
  output [31:0] BusB
);

  wire and_1_out, and_2_out, and_3_out, and_4_out, and_5_out, and_6_out, and_7_out, and_8_out,
       decoder_1_out0, decoder_1_out1, decoder_1_out2, decoder_1_out3, decoder_1_out4, decoder_1_out5,
       decoder_1_out6, decoder_1_out7, decoder_2_out0, decoder_2_out1, decoder_2_out2, decoder_2_out3,
       decoder_2_out4, decoder_2_out5, decoder_2_out6, decoder_2_out7, decoder_3_out0, decoder_3_out1,
       decoder_3_out2, decoder_3_out3, decoder_3_out4, decoder_3_out5, decoder_3_out6, decoder_3_out7;
  wire [31:0] R0_q, R1_q, R2_q, R3_q, R4_q, R5_q, R6_q, R7_q;

  Decoder #(.select(3), .enable("false")) decoder_1 (
    .out0(decoder_1_out0), .out1(decoder_1_out1), .out2(decoder_1_out2), .out3(decoder_1_out3),
    .out4(decoder_1_out4), .out5(decoder_1_out5), .out6(decoder_1_out6), .out7(decoder_1_out7), .sel(RW));
  and and_1 (and_1_out, decoder_1_out0, RegWrite);
  and and_2 (and_2_out, decoder_1_out1, RegWrite);
  and and_3 (and_3_out, decoder_1_out2, RegWrite);
  and and_4 (and_4_out, decoder_1_out3, RegWrite);
  and and_5 (and_5_out, decoder_1_out4, RegWrite);
  and and_6 (and_6_out, decoder_1_out5, RegWrite);
  and and_7 (and_7_out, decoder_1_out6, RegWrite);
  and and_8 (and_8_out, decoder_1_out7, RegWrite);
  Register #(.width(32)) R0 (.D(BusW), .en(and_1_out), .Q(R0_q), .clk(CLK));  // open: clr
  Register #(.width(32)) R1 (.D(BusW), .en(and_2_out), .Q(R1_q), .clk(CLK));  // open: clr
  Register #(.width(32)) R2 (.D(BusW), .en(and_3_out), .Q(R2_q), .clk(CLK));  // open: clr
  Register #(.width(32)) R3 (.D(BusW), .en(and_4_out), .Q(R3_q), .clk(CLK));  // open: clr
  Register #(.width(32)) R4 (.D(BusW), .en(and_5_out), .Q(R4_q), .clk(CLK));  // open: clr
  Register #(.width(32)) R5 (.D(BusW), .en(and_6_out), .Q(R5_q), .clk(CLK));  // open: clr
  Register #(.width(32)) R6 (.D(BusW), .en(and_7_out), .Q(R6_q), .clk(CLK));  // open: clr
  Register #(.width(32)) R7 (.D(BusW), .en(and_8_out), .Q(R7_q), .clk(CLK));  // open: clr
  // Probe on BusA
  Decoder #(.select(3), .enable("false")) decoder_2 (
    .out0(decoder_2_out0), .out1(decoder_2_out1), .out2(decoder_2_out2), .out3(decoder_2_out3),
    .out4(decoder_2_out4), .out5(decoder_2_out5), .out6(decoder_2_out6), .out7(decoder_2_out7), .sel(RA));
  assign BusA = decoder_2_out0 ? R0_q : 32'bz;  // Controlled_Buffer controlled_buffer_1
  assign BusA = decoder_2_out1 ? R1_q : 32'bz;  // Controlled_Buffer controlled_buffer_2
  assign BusA = decoder_2_out2 ? R2_q : 32'bz;  // Controlled_Buffer controlled_buffer_3
  assign BusA = decoder_2_out3 ? R3_q : 32'bz;  // Controlled_Buffer controlled_buffer_4
  assign BusA = decoder_2_out4 ? R4_q : 32'bz;  // Controlled_Buffer controlled_buffer_5
  assign BusA = decoder_2_out5 ? R5_q : 32'bz;  // Controlled_Buffer controlled_buffer_6
  assign BusA = decoder_2_out6 ? R6_q : 32'bz;  // Controlled_Buffer controlled_buffer_7
  assign BusA = decoder_2_out7 ? R7_q : 32'bz;  // Controlled_Buffer controlled_buffer_8
  Decoder #(.select(3), .enable("false")) decoder_3 (
    .out0(decoder_3_out0), .out1(decoder_3_out1), .out2(decoder_3_out2), .out3(decoder_3_out3),
    .out4(decoder_3_out4), .out5(decoder_3_out5), .out6(decoder_3_out6), .out7(decoder_3_out7), .sel(RB));
  assign BusB = decoder_3_out0 ? R0_q : 32'bz;  // Controlled_Buffer controlled_buffer_9
  assign BusB = decoder_3_out1 ? R1_q : 32'bz;  // Controlled_Buffer controlled_buffer_10
  assign BusB = decoder_3_out2 ? R2_q : 32'bz;  // Controlled_Buffer controlled_buffer_11
  assign BusB = decoder_3_out3 ? R3_q : 32'bz;  // Controlled_Buffer controlled_buffer_12
  assign BusB = decoder_3_out4 ? R4_q : 32'bz;  // Controlled_Buffer controlled_buffer_13
  assign BusB = decoder_3_out5 ? R5_q : 32'bz;  // Controlled_Buffer controlled_buffer_14
  assign BusB = decoder_3_out6 ? R6_q : 32'bz;  // Controlled_Buffer controlled_buffer_15
  assign BusB = decoder_3_out7 ? R7_q : 32'bz;  // Controlled_Buffer controlled_buffer_16
  // Probe on BusB
endmodule

module ALU (
  input  [31:0] A,
  input  [31:0] B,
  input  [3:0] ALUCntl,
  output [31:0] ALU_out,
  output Sign,
  output Zero
);

  wire comparator_2_lt, comparator_3_lt, multiplexer_2_out;
  wire [31:0] adder_1_out, AND_out, bit_extender_1_out, bit_extender_2_out, CAND_out, multiplexer_1_out,
       multiplexer_3_out, not_1_out, OR_out, shifter_1_out, shifter_2_out, shifter_3_out, shifter_4_out,
       xor_1_out, XOR_2_out;

  // Probe on B
  assign bit_extender_1_out = {{31{ALUCntl[2]}}, ALUCntl[2]};  // Bit_Extender bit_extender_1
  // Probe on A
  assign xor_1_out = A ^ bit_extender_1_out;  // XOR_Gate xor_1, 32 bits wide
  assign not_1_out = ~A;  // NOT_Gate not_1, 32 bits wide
  Comparator #(.width(32)) comparator_1 (.a(A), .b({32{1'b0}}), .eq(Zero));  // open: gt, lt
  Adder #(.width(32)) adder_1 (.a(B), .b(xor_1_out), .out(adder_1_out), .cin(ALUCntl[2]));  // open: cout
  // Probe on adder_1_out
  assign CAND_out = not_1_out & B;  // AND_Gate CAND, 32 bits wide
  assign AND_out = A & B;  // AND_Gate AND, 32 bits wide
  assign OR_out = A | B;  // OR_Gate OR, 32 bits wide
  assign XOR_2_out = A ^ B;  // XOR_Gate XOR_2, 32 bits wide
  Multiplexer #(.select(2), .width(32), .enable("false")) multiplexer_1 (
    .in0(AND_out), .in1(CAND_out), .in2(OR_out), .in3(XOR_2_out), .out(multiplexer_1_out), .sel(ALUCntl[3:2]));
  Comparator #(.width(32)) comparator_2 (.a(A), .b(B), .lt(comparator_2_lt));  // open: gt, eq
  Comparator #(.width(32), .mode("unsigned")) comparator_3 (.a(A), .b(B), .lt(comparator_3_lt));  // open: gt, eq
  Shifter #(.width(32), .shift("rr")) shifter_1 (.in(A), .\dist (B[4:0]), .out(shifter_1_out));
  Shifter #(.width(32)) shifter_2 (.in(A), .\dist (B[4:0]), .out(shifter_2_out));
  Shifter #(.width(32), .shift("lr")) shifter_3 (.in(A), .\dist (B[4:0]), .out(shifter_3_out));
  Shifter #(.width(32), .shift("ar")) shifter_4 (.in(A), .\dist (B[4:0]), .out(shifter_4_out));
  Multiplexer #(.enable("false")) multiplexer_2 (
    .in0(comparator_2_lt), .in1(comparator_3_lt), .out(multiplexer_2_out), .sel(ALUCntl[2]));
  assign bit_extender_2_out = {{31{1'b0}}, multiplexer_2_out};  // Bit_Extender bit_extender_2
  Multiplexer #(.select(2), .width(32), .enable("false")) multiplexer_3 (
    .in0(shifter_1_out), .in1(shifter_2_out), .in2(shifter_3_out), .in3(shifter_4_out),
    .out(multiplexer_3_out), .sel(ALUCntl[3:2]));
  Multiplexer #(.select(2), .width(32), .enable("false")) multiplexer_4 (
    .in0(multiplexer_3_out), .in1(bit_extender_2_out), .in2(adder_1_out), .in3(multiplexer_1_out),
    .out(ALU_out), .sel(ALUCntl[1:0]));

  assign Sign = ALU_out[31];

  // Other names for the same wires on the sheet: OP_1[1:0] = ALUCntl[3:2]; OP_3 = ALUCntl[2];
  //   OP_2[1:0] = ALUCntl[1:0]; ResultR[31:0] = ALU_out

  // Notes on the sheet:
  //   ADD = 0
  //   SUB = 1
  //   CAND = 00
  //   AND = 01
  //   OR = 10
  //   XOR = 11
  //   UnsignedOp
  //   SLT = 0
  //   SLTU = 1
  //   ROR = 00
  //   SLL = 01
  //   SRL = 10
  //   SRA = 11
  //   Shift = 00
  //   Slt = 01
  //   Add/ Sub = 10
  //   Logic = 11
endmodule

module PCNext (
  input  jump,
  input  jal,
  input  JALR,
  input  Jr,
  input  Bgtz,
  input  Zero,
  input  Bnez,
  input  Beqz,
  input  Bgez,
  input  Bltz,
  input  Blez,
  input  Sign,
  output [1:0] PCSrc
);

  wire and_1_out, and_2_out, and_3_out, and_4_out, and_5_out, and_6_out, and_7_out, not_1_out, not_2_out,
       not_3_out, not_4_out, or_1_out, or_2_out, or_3_out, or_4_out;

  and and_1 (and_1_out, Bgtz, and_2_out);
  and and_2 (and_2_out, not_2_out, not_1_out);
  not not_1 (not_1_out, Zero);
  not not_2 (not_2_out, Sign);
  or or_1 (or_1_out, jump, jal);
  and and_3 (and_3_out, or_2_out, Blez);
  or or_2 (or_2_out, Zero, Sign);
  Priority_Encoder #(.select(2)) priority_encoder_1 (
    .in0(1'b1), .in1(or_1_out), .in2(or_3_out), .in3(or_4_out), .out(PCSrc));
  or or_3 (or_3_out, and_1_out, and_3_out, and_4_out, and_5_out, and_6_out, and_7_out);
  and and_4 (and_4_out, not_3_out, Bnez);
  not not_3 (not_3_out, Zero);
  and and_5 (and_5_out, Zero, Beqz);
  or or_4 (or_4_out, JALR, Jr);
  and and_6 (and_6_out, Bgez, not_4_out);
  not not_4 (not_4_out, Sign);
  and and_7 (and_7_out, Sign, Bltz);
endmodule

module ControUnit (
  input  [1:0] Function,
  input  [4:0] OpCode,
  output RegDst,
  output RegWrite,
  output ExtOp,
  output ALUSrc,
  output Beqz,
  output Bnez,
  output MemRead,
  output [3:0] ALUCtrl,
  output MemWrite,
  output MemtoReg,
  output J,
  output Jal,
  output Jr,
  output Bltz,
  output Bgez,
  output Bgtz,
  output Blez,
  output Jalr,
  output SET,
  output SSET
);

  wire nor_1_out, nor_2_out, not_1_out;
  wire [5:0] adder_1_out, bit_extender_1_out, multiplexer_1_out, multiplexer_2_out;

  assign bit_extender_1_out = {{1{1'b0}}, OpCode};  // Bit_Extender bit_extender_1
  Adder #(.width(6)) adder_1 (.a(bit_extender_1_out), .b(6'b000110), .out(adder_1_out));  // open: cin, cout
  Multiplexer #(.width(6), .enable("false")) multiplexer_1 (
    .in0(adder_1_out), .in1({4'b0001, Function}), .out(multiplexer_1_out), .sel(nor_1_out));
  nor nor_1 (nor_1_out, OpCode[4], OpCode[3], OpCode[2], OpCode[1], not_1_out);
  not not_1 (not_1_out, OpCode[0]);
  Multiplexer #(.width(6), .enable("false")) multiplexer_2 (
    .in0(multiplexer_1_out), .in1({4'b0000, Function}), .out(multiplexer_2_out), .sel(nor_2_out));
  nor nor_2 (nor_2_out, OpCode[4], OpCode[3], OpCode[2], OpCode[1], OpCode[0]);
  ROM #(.addrWidth(6), .dataWidth(23)) rom_1 (
    .addr(multiplexer_2_out),
    .data({SSET, SET, Jalr, Blez, Bgtz, Bgez, Bltz, Jr, Jal, J, MemtoReg, MemWrite, MemRead, Bnez, Beqz, ALUCtrl, ALUSrc, ExtOp, RegWrite, RegDst}));  // open: sel

  // Notes on the sheet:
  //   contents of rom_1 (hex, n*v repeats v):
  //   33 73 b3 f3 23 63 13 53 0 0 3e 7e be fe 2e 6e 1e 5e 4e 8e ce e 142e 82c 0 0 104 204 10004 20004
  //   40004 80004 8004 100007 20000f 40004b 2004 4007
endmodule
